# Fritzing sketch usb_dac_device (saved by Fritzing 0.7.1b)

parts:
  Part1 = Arduino ProtoShield
  IC1 = IC, DIP package, 8 pins [chip_label="MCP 4822" spacing=300mil]

nets:
  N1: Part1.D9, Part1.N$136, IC1.pin5
  N2: Part1.D10, Part1.N$107, IC1.pin2
  N3: Part1.D11, Part1.N$129, IC1.pin4
  N4: Part1.D13, Part1.N$118, IC1.pin3
  N5: Part1.5V, Part1.N$96, IC1.pin1
  N6: Part1.GND, Part1.N$114, IC1.pin7
  N7: Part1.N$103, IC1.pin8
  N8: Part1.N$125, IC1.pin6
